// Logisim project rudimentary computing device.circ as structural Verilog: 1 circuit, main circuit main
module main (
  input  [17:0] in_1,
  input  in_2,
  input  in_3,
  input  in_4,
  input  in_5,
  input  in_6,
  input  in_7
);

  wire button_1_out, clock_1_out, main_2_add, main_3_out_14, main_3_out_15, main_3_out_16, main_3_out_17,
       main_3_out_18, main_3_out_19, main_4_out_13, main_4_out_14, main_4_out_16, main_4_out_17,
       main_4_out_18, main_4_output, main_5_out_38, main_5_out_39, main_5_out_40, main_5_out_41,
       main_5_out_42, main_5_out_43, main_5_out_44, main_5_out_45, main_5_out_46, main_5_out_47,
       main_5_out_48, main_5_out_49, main_6_out_13, main_6_out_14, main_6_out_16, main_6_out_17,
       main_6_out_18, main_6_output, main_7_out_13, main_7_out_14, main_7_out_16, main_7_out_17,
       main_7_out_18, main_7_output;
  wire [5:0] main_1_out_14;
  wire [18:0] rom_1_data;

  Clock clock_1 (.out(clock_1_out));
  LED led_1 (.in(main_1_out_14[4]));
  LED led_2 (.in(main_1_out_14[5]));
  Button button_1 (.out(button_1_out));
  LED led_3 (.in(main_1_out_14[2]));
  LED led_4 (.in(main_1_out_14[1]));
  LED led_5 (.in(main_1_out_14[0]));
  LED led_6 (.in(main_1_out_14[3]));
  program_counter_main main_1 (
    .in_7(button_1_out), .in_8(clock_1_out), .out_9(main_1_out_14[5]), .out_10(main_1_out_14[4]),
    .out_11(main_1_out_14[3]), .out_12(main_1_out_14[2]), .out_13(main_1_out_14[1]),
    .out_14(main_1_out_14[0]), .in_1(in_2), .in_2(in_3), .in_3(in_4), .in_4(in_5), .in_5(in_6), .in_6(in_7));
  instructor_main main_2 (
    .in_1(rom_1_data[18]), .in_2(rom_1_data[17]), .in_3(rom_1_data[16]), .in_4(rom_1_data[15]),
    .ADD(main_2_add));  // open: INVERT, A_B, A_B_2, A_B_3, STEP, INSERT, OUT, HALT, out_14, out_15, out_16
  addition_main main_3 (
    .in_1(main_5_out_44), .in_2(main_5_out_45), .in_3(main_5_out_46), .in_4(main_5_out_47),
    .in_5(main_5_out_48), .in_6(main_5_out_49), .in_7(main_5_out_38), .in_8(main_5_out_39),
    .in_9(main_5_out_40), .in_10(main_5_out_41), .in_11(main_5_out_42), .in_12(main_5_out_43),
    .out_14(main_3_out_14), .out_15(main_3_out_15), .out_16(main_3_out_16), .out_17(main_3_out_17),
    .out_18(main_3_out_18), .out_19(main_3_out_19));  // open: out_13
  ROM #(.addrWidth(6), .dataWidth(19)) rom_1 (.addr(main_1_out_14), .data(rom_1_data));  // open: sel
  memory_main main_4 (
    .Address(rom_1_data[14]), .in_2(rom_1_data[13]), .Write(rom_1_data[12]), .in_4(rom_1_data[11]),
    .Read(rom_1_data[10]), .Initialise(button_1_out), .in_7(in_1[0]), .in_8(in_1[1]), .Input(in_1[2]),
    .in_10(in_1[3]), .in_11(in_1[4]), .in_12(in_1[5]), .out_13(main_4_out_13), .out_14(main_4_out_14),
    .Output(main_4_output), .out_16(main_4_out_16), .out_17(main_4_out_17), .out_18(main_4_out_18));
  select_input_output_bus_main main_5 (
    .in_20(main_4_out_13), .in_21(main_4_out_14), .in_22(main_4_output), .in_23(main_4_out_16),
    .in_24(main_4_out_17), .in_25(main_4_out_18), .in_1(1'b0), .in_2(1'b0), .in_3(1'b0), .in_4(1'b0),
    .in_5(1'b0), .in_6(1'b0), .in_19(main_2_add), .out_38(main_5_out_38), .out_39(main_5_out_39),
    .out_40(main_5_out_40), .out_41(main_5_out_41), .out_42(main_5_out_42), .out_43(main_5_out_43),
    .in_7(1'b0), .in_26(main_6_out_13), .out_44(main_5_out_44), .in_8(1'b0), .in_27(main_6_out_14),
    .out_45(main_5_out_45), .in_9(1'b0), .in_28(main_6_output), .out_46(main_5_out_46), .in_10(1'b0),
    .in_29(main_6_out_16), .out_47(main_5_out_47), .in_11(1'b0), .in_30(main_6_out_17),
    .out_48(main_5_out_48), .in_12(1'b0), .in_31(main_6_out_18), .out_49(main_5_out_49), .in_13(1'b0),
    .in_32(main_7_out_13), .out_50(main_3_out_14), .in_14(1'b0), .in_33(main_7_out_14),
    .out_51(main_3_out_15), .in_15(1'b0), .in_34(main_7_output), .out_52(main_3_out_16), .in_16(1'b0),
    .in_35(main_7_out_16), .out_53(main_3_out_17), .in_17(1'b0), .in_36(main_7_out_17),
    .out_54(main_3_out_18), .in_18(1'b0), .in_37(main_7_out_18), .out_55(main_3_out_19));
  memory_main main_6 (
    .Address(rom_1_data[9]), .in_2(rom_1_data[8]), .Write(rom_1_data[7]), .in_4(rom_1_data[6]),
    .Read(rom_1_data[5]), .Initialise(button_1_out), .in_7(in_1[6]), .in_8(in_1[7]), .Input(in_1[8]),
    .in_10(in_1[9]), .in_11(in_1[10]), .in_12(in_1[11]), .out_13(main_6_out_13), .out_14(main_6_out_14),
    .Output(main_6_output), .out_16(main_6_out_16), .out_17(main_6_out_17), .out_18(main_6_out_18));
  memory_main main_7 (
    .Address(rom_1_data[4]), .in_2(rom_1_data[3]), .Write(rom_1_data[2]), .in_4(rom_1_data[1]),
    .Read(rom_1_data[0]), .Initialise(button_1_out), .in_7(in_1[12]), .in_8(in_1[13]), .Input(in_1[14]),
    .in_10(in_1[15]), .in_11(in_1[16]), .in_12(in_1[17]), .out_13(main_7_out_13), .out_14(main_7_out_14),
    .Output(main_7_output), .out_16(main_7_out_16), .out_17(main_7_out_17), .out_18(main_7_out_18));

  // Notes on the sheet:
  //   contents of rom_1 (hex, n*v repeats v):
  //   39800 380c0 94a6 40005 5 6 7 8 9 a b c d e f
endmodule
